// Logisim project TallerParcial.circ as structural Verilog: 9 circuits, main circuit sumador_simple
module sumador_simple (
  input  A,
  input  B,
  output S,
  output Cout
);

  xor xor_1 (S, A, B);
  and and_1 (Cout, B, A);
endmodule

module sumador_completo (
  input  Cin,
  input  A,
  input  B,
  output S,
  output Cout
);

  wire sumador_simple_1_cout, sumador_simple_1_s, sumador_simple_2_cout;

  sumador_simple sumador_simple_1 (.A(A), .B(B), .S(sumador_simple_1_s), .Cout(sumador_simple_1_cout));
  sumador_simple sumador_simple_2 (.A(sumador_simple_1_s), .B(Cin), .S(S), .Cout(sumador_simple_2_cout));
  or or_1 (Cout, sumador_simple_2_cout, sumador_simple_1_cout);
endmodule

module sumador_4 (
  input  Cin,
  input  [3:0] A,
  input  [3:0] B,
  output [3:0] S,
  output Cout
);

  wire sumador_completo_1_cout, sumador_completo_2_cout, sumador_completo_3_cout;

  sumador_completo sumador_completo_1 (
    .Cin(sumador_completo_3_cout), .A(A[2]), .B(B[2]), .S(S[2]), .Cout(sumador_completo_1_cout));
  sumador_completo sumador_completo_2 (.Cin(Cin), .A(A[0]), .B(B[0]), .S(S[0]), .Cout(sumador_completo_2_cout));
  sumador_completo sumador_completo_3 (
    .Cin(sumador_completo_2_cout), .A(A[1]), .B(B[1]), .S(S[1]), .Cout(sumador_completo_3_cout));
  sumador_completo sumador_completo_4 (.Cin(sumador_completo_1_cout), .A(A[3]), .B(B[3]), .S(S[3]), .Cout(Cout));
  Hex_Digit_Display hex_digit_display_1 (.value(S));  // open: dp
endmodule

module comparador_cero (
  input  [3:0] A,
  output Z
);

  wire or_1_out, or_2_out, or_3_out;

  or or_1 (or_1_out, A[0], A[1]);
  or or_2 (or_2_out, A[2], A[3]);
  or or_3 (or_3_out, or_1_out, or_2_out);
  not not_1 (Z, or_3_out);
endmodule

module sumador_flags (
  input  Cin,
  input  [3:0] A,
  input  [3:0] B,
  output [3:0] S,
  output N,
  output Z,
  output V,
  output C
);

  wire and_1_out, and_2_out, and_3_out, and_4_out, not_1_out, not_2_out, not_3_out;

  not not_1 (not_1_out, B[3]);
  not not_2 (not_2_out, A[3]);
  and and_1 (and_1_out, B[3], A[3]);
  and and_2 (and_2_out, not_1_out, not_2_out);
  sumador_4 sumador_4_1 (.Cin(Cin), .A(A), .B(B), .S({N, S[2:0]}), .Cout(C));
  not not_3 (not_3_out, N);
  and and_3 (and_3_out, not_3_out, and_1_out);
  and and_4 (and_4_out, N, and_2_out);
  or or_1 (V, and_3_out, and_4_out);
  Hex_Digit_Display hex_digit_display_1 (.value({N, S[2:0]}));  // open: dp
  comparador_cero comparador_cero_1 (.A({N, S[2:0]}), .Z(Z));

  assign S[3] = N;
endmodule

module incrementador_4 (
  input  [3:0] A,
  output [3:0] S
);

  sumador_4 sumador_4_1 (.A(A), .B(4'b0001), .S(S));  // open: Cin, Cout
  Hex_Digit_Display hex_digit_display_1 (.value(S));  // open: dp
endmodule

module inversor_4 (
  input  [3:0] A,
  input  INV,
  output [3:0] S
);

  wire [3:0] xor_1_out;

  xor xor_1 (xor_1_out[0], INV, A[0]);
  xor xor_2 (xor_1_out[1], A[1], INV);
  xor xor_3 (xor_1_out[2], A[2], INV);
  xor xor_4 (xor_1_out[3], A[3], INV);
  Hex_Digit_Display hex_digit_display_1 (.value(S));  // open: dp
  sumador_4 sumador_4_1 (.Cin(INV), .A(xor_1_out), .S(S));  // open: B, Cout
endmodule

module ALU (
  input  [3:0] A,
  input  [3:0] B,
  input  [1:0] OP,
  output N,
  output Z,
  output V,
  output C,
  output [3:0] S
);

  wire comparador_cero_1_z, comparador_cero_2_z, multiplexer_3_out, not_1_out, not_2_out, sumador_flags_1_c,
       sumador_flags_1_n, sumador_flags_1_v, sumador_flags_1_z, sumador_flags_2_c, sumador_flags_2_n,
       sumador_flags_2_v, sumador_flags_2_z;
  wire [3:0] and_1_out, demultiplexer_1_out0, demultiplexer_1_out1, demultiplexer_1_out2,
       demultiplexer_1_out3, demultiplexer_2_out0, demultiplexer_2_out1, demultiplexer_2_out2,
       demultiplexer_2_out3, inversor_4_1_s, or_1_out, sumador_flags_1_s, sumador_flags_2_s;

  Demultiplexer #(.select(2), .width(4)) demultiplexer_1 (
    .out0(demultiplexer_1_out0), .out1(demultiplexer_1_out1), .out2(demultiplexer_1_out2),
    .out3(demultiplexer_1_out3), .in(A), .sel(OP));
  Demultiplexer #(.select(2), .width(4)) demultiplexer_2 (
    .out0(demultiplexer_2_out0), .out1(demultiplexer_2_out1), .out2(demultiplexer_2_out2),
    .out3(demultiplexer_2_out3), .in(B), .sel(OP));
  and and_1 (and_1_out[0], demultiplexer_2_out2[0], demultiplexer_1_out2[0]);
  and and_2 (and_1_out[1], demultiplexer_2_out2[1], demultiplexer_1_out2[1]);
  and and_3 (and_1_out[2], demultiplexer_2_out2[2], demultiplexer_1_out2[2]);
  and and_4 (and_1_out[3], demultiplexer_2_out2[3], demultiplexer_1_out2[3]);
  or or_1 (or_1_out[0], demultiplexer_1_out3[0], demultiplexer_2_out3[0]);
  or or_2 (or_1_out[1], demultiplexer_1_out3[1], demultiplexer_2_out3[1]);
  or or_3 (or_1_out[2], demultiplexer_1_out3[2], demultiplexer_2_out3[2]);
  or or_4 (or_1_out[3], demultiplexer_1_out3[3], demultiplexer_2_out3[3]);
  inversor_4 inversor_4_1 (.A(demultiplexer_2_out1), .INV(1'b1), .S(inversor_4_1_s));
  sumador_flags sumador_flags_1 (
    .A(demultiplexer_1_out0), .B(demultiplexer_2_out0), .S(sumador_flags_1_s), .N(sumador_flags_1_n),
    .Z(sumador_flags_1_z), .V(sumador_flags_1_v), .C(sumador_flags_1_c));  // open: Cin
  sumador_flags sumador_flags_2 (
    .A(demultiplexer_1_out1), .B(inversor_4_1_s), .S(sumador_flags_2_s), .N(sumador_flags_2_n),
    .Z(sumador_flags_2_z), .V(sumador_flags_2_v), .C(sumador_flags_2_c));  // open: Cin
  comparador_cero comparador_cero_1 (.A(and_1_out), .Z(comparador_cero_1_z));
  Multiplexer #(.select(2)) multiplexer_1 (
    .in0(sumador_flags_1_z), .in1(sumador_flags_2_z), .in2(comparador_cero_1_z), .in3(comparador_cero_2_z),
    .out(Z), .sel(OP));
  not not_1 (not_1_out, sumador_flags_2_c);
  comparador_cero comparador_cero_2 (.A(or_1_out), .Z(comparador_cero_2_z));
  Multiplexer #(.select(2)) multiplexer_2 (
    .in0(sumador_flags_1_n), .in1(sumador_flags_2_n), .in2(and_1_out[3]), .in3(or_1_out[3]), .out(N), .sel(OP));
  Multiplexer #(.select(2)) multiplexer_3 (
    .in0(sumador_flags_1_c), .in1(not_1_out), .in2(1'b0), .in3(1'b0), .out(multiplexer_3_out), .sel(OP));
  Multiplexer #(.select(2), .width(4)) multiplexer_4 (
    .in0(sumador_flags_1_s), .in1(sumador_flags_2_s), .in2(and_1_out), .in3(or_1_out), .out(S), .sel(OP));
  Multiplexer #(.select(2)) multiplexer_5 (
    .in0(sumador_flags_1_v), .in1(sumador_flags_2_v), .in2(1'b0), .in3(1'b0), .out(V), .sel(OP));
  not not_2 (not_2_out, V);
  and and_5 (C, not_2_out, multiplexer_3_out);
  Hex_Digit_Display hex_digit_display_1 (.value(S));  // open: dp
endmodule

module verificador (
  output [3:0] out_1,
  output [3:0] out_2,
  output [1:0] out_3,
  output halt,
  output N,
  output Z,
  output V,
  output C,
  output [3:0] res
);

  wire clock_1_out;

  Clock clock_1 (.out(clock_1_out));
  Counter #(.max('h3ff), .width(10)) counter_1 (
    .clk(clock_1_out), .carry(halt), .Q({out_3, out_2, out_1}));  // open: clr, load, up, count, D
  ALU alu_1 (.A(out_1), .B(out_2), .OP(out_3), .N(N), .Z(Z), .V(V), .C(C), .S(res));
endmodule
